// Logisim project D FLIPFLOP.circ as structural Verilog: 1 circuit, main circuit main
module main (
  input  D,
  output Q,
  output Q_
);

  wire CLOCK_out;

  Clock CLOCK (.out(CLOCK_out));
  D_Flip_Flop d_ff_1 (.clk(CLOCK_out), .D(D), .Q(Q), .Qn(Q_));  // open: preset, en, reset

  // Notes on the sheet:
  //   D=0  Q=0   Q_ =1
  //   D = 1  Q =1   Q_= 
endmodule
