// Logisim project EXP - 7 BCD UO COUNTER.circ as structural Verilog: 1 circuit, main circuit main
module main (
  input  in_1,
  output Q0,
  output Q1,
  output Q2,
  output Q3
);

  wire and_1_out, clock_1_out;

  Clock clock_1 (.out(clock_1_out));
  J_K_Flip_Flop FF0 (.J(in_1), .clk(clock_1_out), .K(in_1), .Q(Q0), .reset(and_1_out));  // open: Qn, preset, en
  J_K_Flip_Flop FF1 (.J(in_1), .clk(Q0), .K(in_1), .Q(Q1), .reset(and_1_out));  // open: Qn, preset, en
  J_K_Flip_Flop FF2 (.J(in_1), .clk(Q1), .K(in_1), .Q(Q2), .reset(and_1_out));  // open: Qn, preset, en
  J_K_Flip_Flop FF3 (.J(in_1), .clk(Q2), .K(in_1), .Q(Q3), .reset(and_1_out));  // open: Qn, preset, en
  and and_1 (and_1_out, Q1, Q3);

  // Notes on the sheet:
  //   LOGIC DIAGRAM OF 4-BIT BCD UP COUNTER :
endmodule
