// Logisim project EXP - 7 BINARY DOWN COUNTER.circ as structural Verilog: 1 circuit, main circuit main
module main (
  input  in_1,
  output Q0,
  output Q1,
  output Q2,
  output Q3
);

  wire clock_1_out, FF0_qn, FF1_qn, FF2_qn;

  Clock clock_1 (.out(clock_1_out));
  J_K_Flip_Flop FF0 (.J(in_1), .clk(clock_1_out), .K(in_1), .Q(Q0), .Qn(FF0_qn));  // open: preset, en, reset
  J_K_Flip_Flop FF1 (.J(in_1), .clk(FF0_qn), .K(in_1), .Q(Q1), .Qn(FF1_qn));  // open: preset, en, reset
  J_K_Flip_Flop FF2 (.J(in_1), .clk(FF1_qn), .K(in_1), .Q(Q2), .Qn(FF2_qn));  // open: preset, en, reset
  J_K_Flip_Flop FF3 (.J(in_1), .clk(FF2_qn), .K(in_1), .Q(Q3));  // open: Qn, preset, en, reset

  // Notes on the sheet:
  //   LOGIC DIAGRAM OF 4-BIT BINARY DOWN  COUNTER :
endmodule
