// Logisim project EXP - 7 BINARY UP COUNTER.circ as structural Verilog: 1 circuit, main circuit main
module main (
  input  in_1,
  output Q0,
  output Q1,
  output Q2,
  output Q3
);

  wire clock_1_out;

  Clock clock_1 (.out(clock_1_out));
  J_K_Flip_Flop FF1 (.J(in_1), .clk(clock_1_out), .K(in_1), .Q(in_1));  // open: Qn, preset, en, reset
  J_K_Flip_Flop FF2 (.J(in_1), .clk(in_1), .Q(in_1));  // open: K, Qn, preset, en, reset
  J_K_Flip_Flop FF3 (.J(in_1), .clk(in_1), .Q(Q2));  // open: K, Qn, preset, en, reset
  J_K_Flip_Flop FF4 (.J(in_1), .clk(Q2), .K(in_1), .Q(Q3));  // open: Qn, preset, en, reset

  assign Q0 = in_1;
  assign Q1 = in_1;

  // Notes on the sheet:
  //   LOGIC DIAGRAM OF 4-BIT BINARY UP COUNTER :
endmodule
