// Logisim project EXP-8.circ as structural Verilog: 1 circuit, main circuit main
module main (
  input  [7:0] INPUT_A,
  input  [7:0] INPUT_B,
  input  [2:0] SELECTION_INPUT,
  input  [2:0] NO_OF_SHIFTS___ROTATES,
  output CARRY_OUT_ADDITION_OPERATION,
  output BORROW_OUTSUBRACTION_OPRATION,
  output [7:0] UPPER_BYTE_MULTIPLICATION_OPERATION,
  output [7:0] OUTPUT
);

  wire [7:0] adder_1_out, and_1_out, multiplier_1_out, nor_1_out, shifter_1_out, shifter_2_out,
       subtractor_1_out, xor_1_out;

  Adder adder_1 (.a(INPUT_A), .b(INPUT_B), .out(adder_1_out), .cout(CARRY_OUT_ADDITION_OPERATION));  // open: cin
  Subtractor subtractor_1 (
    .a(INPUT_A), .b(INPUT_B), .out(subtractor_1_out), .bout(BORROW_OUTSUBRACTION_OPRATION));  // open: bin
  Multiplier multiplier_1 (.out(multiplier_1_out), .cout(UPPER_BYTE_MULTIPLICATION_OPERATION));  // open: a, b, cin
  assign and_1_out = INPUT_A & INPUT_B;  // AND_Gate and_1, 8 bits wide
  assign nor_1_out = ~(INPUT_A | INPUT_B);  // NOR_Gate nor_1, 8 bits wide
  assign xor_1_out = INPUT_A ^ INPUT_B;  // XOR_Gate xor_1, 8 bits wide
  Shifter #(.shift("lr")) shifter_1 (.in(INPUT_A), .\dist (NO_OF_SHIFTS___ROTATES), .out(shifter_1_out));
  Shifter #(.shift("rl")) shifter_2 (.in(INPUT_A), .\dist (NO_OF_SHIFTS___ROTATES), .out(shifter_2_out));
  Multiplexer #(.select(3), .width(8)) multiplexer_1 (
    .in0(adder_1_out), .in1(subtractor_1_out), .in2(multiplier_1_out), .in3(and_1_out), .in4(nor_1_out),
    .in5(xor_1_out), .in6(shifter_1_out), .in7(shifter_2_out), .out(OUTPUT), .sel(SELECTION_INPUT));  // open: en

  // Notes on the sheet:
  //   1   --> NEGATIVE OPERATION
  //   0  --> POSITIVE NUMBER
endmodule
