// Logisim project JK FLIPFLOP.circ as structural Verilog: 1 circuit, main circuit main
module main (
  input  J,
  input  K,
  input  PRE,
  input  EN,
  input  CLR,
  output Q,
  output Q_
);

  wire CLK_out;

  Clock CLK (.out(CLK_out));
  J_K_Flip_Flop j_k_ff_1 (.J(J), .clk(CLK_out), .K(K), .Q(Q), .Qn(Q_), .preset(PRE), .en(EN), .reset(CLR));
endmodule
