// Logisim project SR FLIPFLOP.circ as structural Verilog: 1 circuit, main circuit main
module main (
  input  S,
  input  R
);

  wire CLOCK_out, NAND_1_out, NAND_2_out, NAND_3_out, NAND_4_out;

  Clock CLOCK (.out(CLOCK_out));
  nand NAND_1 (NAND_1_out, S, CLOCK_out);
  nand NAND_2 (NAND_2_out, CLOCK_out, R);
  nand NAND_3 (NAND_3_out, NAND_1_out, NAND_4_out);
  nand NAND_4 (NAND_4_out, NAND_3_out, NAND_2_out);

  // Notes on the sheet:
  //   Q
  //   Q_ BAR
endmodule
